# Fritzing sketch temp design (saved by Fritzing 1.0.6)
breadboards: 1

parts:
  U1 = 7400 4 x 2 Input NAND Gate [part_number=7400 package="DIP (Dual Inline) [THT]"]

nets:
  N1: U1.B1, U1.Q2
  N2: U1.Q1, U1.A2, U1.B4
  N3: U1.B2, U1.B3
  N4: U1.A3, U1.Q4
